# Fritzing sketch BattleBotSchema_0 (saved by Fritzing 0.9.2b)

parts:
  S1 = H-Bridge with L298N
  Part1 = Arduino Uno (Rev3)
  M2 = DC Motor
  M3 = DC Motor
  BAT1 = BC9VPC [package=bc9vpc]
  Keyes1 = Keyes IR Infrared Sensor Switch Module
  Keyes2 = Keyes IR Infrared Sensor Switch Module
  Part2 = Bluetooth HC-05 Macho
  Part3 = SRF05 Ultrasonic Rangefinder
  GY1 = MPU-6050 Board GY-521 [form="♀ (female)" package=THT]
  LCD2 = LCD screen
  LCM1602_IIC2 = LCM1602 IIC [part_number="LCM1602 IIC" chip_label="LCM1602 IIC" package="DIP (Dual Inline) [THT]"]

nets:
  12V: S1.12V, BAT1.V+, GY1.pin1, LCM1602_IIC2.VCC
  N1: S1.GND, BAT1.V-
  N2: S1.IN1, Part1.D2
  N3: S1.IN2, Part1.D3_PWM
  N4: S1.IN3, Part1.D4
  N5: S1.IN4, Part1.D9_PWM
  N6: S1.M1-01, M3.pin_2
  N7: S1.M1-02, M3.pin_1
  N8: S1.M2-01, M2.pin_1
  N9: S1.M2-02, M2.pin_2
  N10: Part1.A0, Part2.TXD
  N11: Part1.A1, Part2.RXD
  N12: Part1.A4/SDA, GY1.pin3, LCM1602_IIC2.SCL
  N13: Part1.A5/SCL, GY1.pin4, LCM1602_IIC2.SDA
  N14: Part1.D10_PWM/SS, Keyes2.VCC
  N15: Part1.D11_PWM/MOSI, Keyes1.VCC
  N16: Part1.D12/MISO, Part3.Echo
  N17: Part1.D13/SCK, Part3.Trig
  GND: Part1.GND, Part2.GND, GY1.pin2, LCM1602_IIC2.GND
  VSS: LCD2.VSS, LCM1602_IIC2.VSS
  VDD: LCD2.VDD, LCM1602_IIC2.VDD
  N18: LCD2.V0, LCM1602_IIC2.V0
  N19: LCD2.RS, LCM1602_IIC2.RS
  N20: LCD2.R/W, LCM1602_IIC2.RW
  N21: LCD2.E, LCM1602_IIC2.E
  N22: LCD2.DB0, LCM1602_IIC2.D0
  N23: LCD2.DB1, LCM1602_IIC2.D1
  N24: LCD2.DB2, LCM1602_IIC2.D2
  N25: LCD2.DB3, LCM1602_IIC2.D3
  N26: LCD2.DB4, LCM1602_IIC2.D4
  N27: LCD2.DB5, LCM1602_IIC2.D5
  N28: LCD2.DB6, LCM1602_IIC2.D6
  N29: LCD2.DB7, LCM1602_IIC2.D7
  N30: LCD2.LED+, LCM1602_IIC2.A
  N31: LCD2.LED-, LCM1602_IIC2.K
  N32: LCM1602_IIC2.LED_A, LCM1602_IIC2.LED_B

custom parts:
  H-Bridge with L298N: h-bridge
  Keyes IR Infrared Sensor Switch Module: An infrared obstacle detector
  MPU-6050 Board GY-521: Acelerometro y Giroscopio MPU-6050 Board GY-521
  LCM1602 IIC: I2C-Module to use a 1602 or 2004 LCD on with the wire.h libory Serial LCD Modul
